# Fritzing sketch rabbit_moto (saved by Fritzing 0.9.3b)
breadboards: 1

parts:
  Part1 = Adafruit TCA9548A
  Part2 = Adafruit DRV2605L [part_number="Adafruit #2305"]
  BeagleBone1 = BeagleBone Black
  Part3 = Adafruit DRV2605L [part_number="Adafruit #2305"]

nets:
  VIN: Part1.VCC, Part2.VIN, BeagleBone1.no_name_yet#3, Part3.VIN
  GND: Part1.GND, Part2.GND, BeagleBone1.no_name_yet#2, Part3.GND
  N1: Part1.INPUTSDA, BeagleBone1.no_name_yet#20
  N2: Part1.INPUTSCL, BeagleBone1.no_name_yet#19
  N3: Part1.0SDA, Part2.SDA
  N4: Part1.0SCL, Part2.SCL
  N5: Part1.1SDA, Part3.SDA
  N6: Part1.1SCL, Part3.SCL

custom parts:
  Adafruit TCA9548A: You just found the perfect I2C sensor, and you want to wire up two or three or more of them to your Arduino when you realize "Uh oh, this chip has a fixed I2C address, and from what I know about I2C, you cannot have two devices with the same address on the same SDA/SCL pins!" Are you out of luck? You would be, if you didn't have this ultra-cool TCA9548A 1-to-8 I2C multiplexer! Finally, a way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
  Adafruit DRV2605L: The DRV2605 from TI is a fancy little motor driver. Rather than controlling a stepper motor or DC motor, its designed specifically for controlling haptic motors - buzzers and vibration motors. Normally one would just turn those kinds of motors on and off, but this driver has the ability to have various effects when driving a vibe motor. For example, ramping the vibration level up and down,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
  BeagleBone Black: BeagleBone Black rev. A5B
